// Logisim project Main.circ as structural Verilog: 9 circuits, main circuit main
module main (
  input  in_1,
  input  [15:0] in_2
);

  wire alu_1_gtz, alu_1_zero, and_1_out, and_2_out, clock_1_out, main_control_unit_1__2nd_reg_source,
       main_control_unit_1_alusrc, main_control_unit_1_bgtz_2, main_control_unit_1_branch,
       main_control_unit_1_jump, main_control_unit_1_link, main_control_unit_1_memread,
       main_control_unit_1_memtoreg, main_control_unit_1_memwrite, main_control_unit_1_reg2pc,
       main_control_unit_1_regdst, main_control_unit_1_regwrite, or_1_out;
  wire [1:0] main_control_unit_1_aluop, multiplexer_2_out;
  wire [3:0] alu_control_unit_1_operation;
  wire [5:0] ram_1_data_2;
  wire [9:0] ram_1_data, shifter_1_out;
  wire [15:0] adder_1_out, adder_2_out, alu_1_out_5, multiplexer_1_out, multiplexer_3_out, multiplexer_4_out,
       multiplexer_5_out, multiplexer_6_out, n4_16_bit_reg_file_1_read_data1,
       n4_16_bit_reg_file_1_read_data2, pc_q, ram_2_data, shifter_2_out, sign_extension_unit_1_out_2;

  Multiplexer #(.width(16)) multiplexer_1 (
    .in0(multiplexer_5_out), .in1(n4_16_bit_reg_file_1_read_data1), .out(multiplexer_1_out),
    .sel(main_control_unit_1_reg2pc));  // open: en
  Clock clock_1 (.out(clock_1_out));
  Register #(.width(16)) pc (.D(multiplexer_1_out), .en(in_1), .Q(pc_q), .clk(clock_1_out));  // open: clr
  Adder #(.width(16)) adder_1 (.a(16'h1), .b(pc_q), .out(adder_1_out));  // open: cin, cout
  Shifter #(.width(10)) shifter_1 (.in(ram_1_data), .\dist (4'b0001), .out(shifter_1_out));
  RAM #(.addrWidth(16), .dataWidth(16)) ram_1 (
    .addr(pc_q), .data({ram_1_data_2, ram_1_data}), .clk(clock_1_out));  // open: sel, ld, clr
  Main_Control_Unit main_control_unit_1 (
    .regdst(main_control_unit_1_regdst), .RegWrite(main_control_unit_1_regwrite),
    .MemtoReg(main_control_unit_1_memtoreg), .MemRead(main_control_unit_1_memread),
    .ALUOp(main_control_unit_1_aluop), .MemWrite(main_control_unit_1_memwrite),
    .ALUSrc(main_control_unit_1_alusrc), .Branch(main_control_unit_1_branch),
    .Jump(main_control_unit_1_jump), .Link(main_control_unit_1_link), .reg2pc(main_control_unit_1_reg2pc),
    .bgtz(ram_1_data_2), .bgtz_2(main_control_unit_1_bgtz_2),
    ._2nd_reg_source(main_control_unit_1__2nd_reg_source));
  Sign_Extension_Unit sign_extension_unit_1 (.in_1(ram_1_data[5:0]), .out_2(sign_extension_unit_1_out_2));
  Multiplexer #(.width(2)) multiplexer_2 (
    .in0(ram_1_data[7:6]), .in1(ram_1_data[5:4]), .out(multiplexer_2_out), .sel(main_control_unit_1_regdst));  // open: en
  ALU_Control_Unit alu_control_unit_1 (
    .ALUOp(main_control_unit_1_aluop), .Funct(ram_1_data[3:0]), .Operation(alu_control_unit_1_operation));
  _4_16_bit_Reg_File u_4_16_bit_reg_file_1 (
    .read_Reg_1(ram_1_data[9:8]), .read_Reg_2(ram_1_data[7:6]), .Write_Register(multiplexer_2_out),
    .Write_Data(multiplexer_6_out), .read_data1(n4_16_bit_reg_file_1_read_data1),
    .read_data2(n4_16_bit_reg_file_1_read_data2), .Link(main_control_unit_1_link),
    .regWrite(main_control_unit_1_regwrite), .return_address(pc_q), .clk(clock_1_out),
    .if_sw_or_lw_always_2nd_reg_as_source(main_control_unit_1__2nd_reg_source));
  Multiplexer #(.width(16)) multiplexer_3 (
    .in0(n4_16_bit_reg_file_1_read_data2), .in1(sign_extension_unit_1_out_2), .out(multiplexer_3_out),
    .sel(main_control_unit_1_alusrc));  // open: en
  Adder #(.width(16)) adder_2 (.a(adder_1_out), .b(shifter_2_out), .out(adder_2_out));  // open: cin, cout
  Shifter #(.width(16)) shifter_2 (.in(sign_extension_unit_1_out_2), .\dist (4'b0010), .out(shifter_2_out));
  ALU alu_1 (
    .fin(n4_16_bit_reg_file_1_read_data1), .zero(alu_1_zero), .out_5(alu_1_out_5), .gtz(alu_1_gtz),
    .sin(multiplexer_3_out), .Operation(alu_control_unit_1_operation));
  and and_1 (and_1_out, main_control_unit_1_branch, alu_1_zero);
  Multiplexer #(.width(16)) multiplexer_4 (
    .in0(adder_1_out), .in1(adder_2_out), .out(multiplexer_4_out), .sel(or_1_out));  // open: en
  and and_2 (and_2_out, main_control_unit_1_bgtz_2, alu_1_gtz);
  RAM #(.addrWidth(16), .dataWidth(16), .bus("separate")) ram_2 (
    .addr(alu_1_out_5), .din(n4_16_bit_reg_file_1_read_data2), .data(ram_2_data),
    .str(main_control_unit_1_memwrite), .clk(clock_1_out), .ld(main_control_unit_1_memread));  // open: sel, clr
  Multiplexer #(.width(16)) multiplexer_5 (
    .in0(multiplexer_4_out), .in1({adder_1_out[15:12], {3{shifter_1_out[9]}}, shifter_1_out[8:0]}),
    .out(multiplexer_5_out), .sel(main_control_unit_1_jump));  // open: en
  or or_1 (or_1_out, and_1_out, and_2_out);
  Multiplexer #(.width(16)) multiplexer_6 (
    .in0(alu_1_out_5), .in1(ram_2_data), .out(multiplexer_6_out), .sel(main_control_unit_1_memtoreg));  // open: en

  // Notes on the sheet:
  //   4bits of next pc
  //   12 bits of given address
  //   <-branch when equal or branch when greater than zero
endmodule

module Sign_Extension_Unit (
  input  [5:0] in_1,
  output [15:0] out_2
);


  assign out_2 = {{11{in_1[5]}}, in_1[4:0]};
endmodule

module _4_16_bit_Reg_File (
  input  Link,
  input  regWrite,
  input  if_sw_or_lw_always_2nd_reg_as_source,
  input  [1:0] read_Reg_1,
  input  [1:0] read_Reg_2,
  input  [1:0] Write_Register,
  input  clk,
  input  [15:0] Write_Data,
  input  [15:0] return_address,
  output [15:0] read_data1,
  output [15:0] read_data2
);

  wire and_1_out, and_2_out, and_3_out, decoder_1_out0, decoder_1_out1, decoder_1_out2, decoder_1_out3;
  wire [15:0] adder_1_out, and_4_out, multiplexer_1_out, register_1_q, register_2_q, register_3_q,
       register_4_q;

  Decoder #(.select(2)) decoder_1 (
    .out0(decoder_1_out0), .out1(decoder_1_out1), .out2(decoder_1_out2), .out3(decoder_1_out3),
    .sel(Write_Register));  // open: en
  and and_1 (and_1_out, decoder_1_out0, regWrite);
  and and_2 (and_2_out, decoder_1_out1, regWrite);
  and and_3 (and_3_out, decoder_1_out2, regWrite);
  Multiplexer #(.width(16)) multiplexer_1 (
    .in0(Write_Data), .in1(return_address), .out(multiplexer_1_out), .sel(Link));  // open: en
  Register #(.width(16)) register_1 (.D(Write_Data), .en(and_1_out), .Q(register_1_q), .clk(clk));  // open: clr
  Register #(.width(16)) register_2 (.D(Write_Data), .en(and_2_out), .Q(register_2_q), .clk(clk));  // open: clr
  Register #(.width(16)) register_3 (.D(Write_Data), .en(and_3_out), .Q(register_3_q), .clk(clk));  // open: clr
  Register #(.width(16)) register_4 (.D(Write_Data), .en(decoder_1_out3), .Q(register_4_q), .clk(clk));  // open: clr
  assign and_4_out = {16{1'b0}} & register_1_q;  // AND_Gate and_4, 16 bits wide
  Adder #(.width(16)) adder_1 (.a(multiplexer_1_out), .b(16'h1), .out(adder_1_out));  // open: cin, cout
  Multiplexer #(.select(2), .width(16)) multiplexer_2 (
    .in0(and_4_out), .in1(register_2_q), .in2(register_3_q), .in3(register_4_q), .out(read_data1),
    .sel(read_Reg_1));  // open: en
  Multiplexer #(.select(2), .width(16)) multiplexer_3 (
    .in0(and_4_out), .in1(register_2_q), .in2(register_3_q), .in3(register_4_q), .out(read_data2),
    .sel(read_Reg_2));  // open: en

  // Notes on the sheet:
  //   output of the register below must be always zero
endmodule

module Main_Control_Unit (
  input  [5:0] bgtz,
  output regdst,
  output RegWrite,
  output MemtoReg,
  output MemRead,
  output [1:0] ALUOp,
  output MemWrite,
  output _2nd_reg_source,
  output ALUSrc,
  output Branch,
  output Jump,
  output Link,
  output reg2pc,
  output bgtz_2
);

  wire addi_out, jmp_out, not_1_out, not_2_out, not_3_out, not_4_out, not_5_out, not_6_out, not_7_out,
       not_8_out, not_9_out, not_10_out, not_11_out, not_12_out, not_13_out, not_14_out, not_15_out,
       not_16_out, not_17_out, not_18_out, not_19_out, not_20_out, not_21_out, not_22_out, not_23_out,
       not_24_out, not_25_out, not_26_out, not_27_out, not_28_out, not_29_out, not_30_out, not_31_out,
       not_32_out, not_33_out, not_34_out, not_35_out, not_36_out, not_37_out, not_38_out, not_39_out;

  not not_1 (not_1_out, bgtz[0]);
  not not_2 (not_2_out, bgtz[1]);
  not not_3 (not_3_out, bgtz[2]);
  and Rtype (ALUOp[1], not_1_out, not_2_out, not_3_out, not_4_out, not_5_out, not_6_out);
  not not_4 (not_4_out, bgtz[3]);
  not not_5 (not_5_out, bgtz[4]);
  not not_6 (not_6_out, bgtz[5]);
  not not_7 (not_7_out, bgtz[2]);
  and lw (MemRead, bgtz[0], bgtz[1], not_7_out, not_8_out, not_9_out, bgtz[5]);
  not not_8 (not_8_out, bgtz[3]);
  not not_9 (not_9_out, bgtz[4]);
  not not_10 (not_10_out, bgtz[2]);
  and sw (MemWrite, bgtz[0], bgtz[1], not_10_out, bgtz[3], not_11_out, bgtz[5]);
  not not_11 (not_11_out, bgtz[4]);
  not not_12 (not_12_out, bgtz[0]);
  not not_13 (not_13_out, bgtz[1]);
  and beq (ALUOp[0], not_12_out, not_13_out, bgtz[2], not_14_out, not_15_out, not_16_out);
  not not_14 (not_14_out, bgtz[3]);
  not not_15 (not_15_out, bgtz[4]);
  not not_16 (not_16_out, bgtz[5]);
  not not_17 (not_17_out, bgtz[0]);
  not not_18 (not_18_out, bgtz[2]);
  and jmp (jmp_out, not_17_out, bgtz[1], not_18_out, not_19_out, not_20_out, not_21_out);
  not not_19 (not_19_out, bgtz[3]);
  not not_20 (not_20_out, bgtz[4]);
  not not_21 (not_21_out, bgtz[5]);
  not not_22 (not_22_out, bgtz[0]);
  not not_23 (not_23_out, bgtz[2]);
  and jal (Link, not_22_out, bgtz[1], not_23_out, not_24_out, not_25_out, bgtz[5]);
  not not_24 (not_24_out, bgtz[3]);
  not not_25 (not_25_out, bgtz[4]);
  not not_26 (not_26_out, bgtz[0]);
  not not_27 (not_27_out, bgtz[1]);
  not not_28 (not_28_out, bgtz[2]);
  and jr (reg2pc, not_26_out, not_27_out, not_28_out, not_29_out, bgtz[4], not_30_out);
  not not_29 (not_29_out, bgtz[3]);
  not not_30 (not_30_out, bgtz[5]);
  not not_31 (not_31_out, bgtz[1]);
  not not_32 (not_32_out, bgtz[2]);
  and u_bgtz (bgtz_2, bgtz[0], not_31_out, not_32_out, not_33_out, not_34_out, bgtz[5]);
  not not_33 (not_33_out, bgtz[3]);
  not not_34 (not_34_out, bgtz[4]);
  not not_35 (not_35_out, bgtz[0]);
  not not_36 (not_36_out, bgtz[1]);
  not not_37 (not_37_out, bgtz[2]);
  and addi (addi_out, not_35_out, not_36_out, not_37_out, bgtz[3], not_38_out, not_39_out);
  not not_38 (not_38_out, bgtz[4]);
  not not_39 (not_39_out, bgtz[5]);
  or or_1 (RegWrite, ALUOp[1], addi_out, MemRead);
  or or_2 (ALUSrc, MemWrite, addi_out, MemRead);
  or or_3 (Jump, jmp_out, Link);
  or or_4 (_2nd_reg_source, MemRead, MemWrite);

  assign Branch = ALUOp[0];
  assign MemtoReg = MemRead;
  assign regdst = ALUOp[1];

  // Notes on the sheet:
  //   aluop1
  //   aluop2
  //   Main Control Unit
endmodule

module ALU_Control_Unit (
  input  [1:0] ALUOp,
  input  [3:0] Funct,
  output [3:0] Operation
);

  wire and_1_out, not_1_out, not_2_out, not_3_out, or_1_out;

  not not_1 (not_1_out, ALUOp[0]);
  and and_1 (and_1_out, ALUOp[1], Funct[1]);
  not not_2 (not_2_out, ALUOp[1]);
  not not_3 (not_3_out, Funct[2]);
  and and_2 (Operation[0], ALUOp[1], or_1_out);
  or or_1 (or_1_out, Funct[3], Funct[0]);
  and and_3 (Operation[3], ALUOp[0], not_1_out);
  or or_2 (Operation[2], ALUOp[0], and_1_out);
  or or_3 (Operation[1], not_2_out, not_3_out);

  // Notes on the sheet:
  //   ALU Control Unit
endmodule

module ALU (
  input  [3:0] Operation,
  input  [15:0] fin,
  input  [15:0] sin,
  output zero,
  output [15:0] out_5,
  output gtz
);

  wire n1_bit_alu_1_cout, n1_bit_alu_2_cout, n1_bit_alu_3_cout, n1_bit_alu_4_cout, n1_bit_alu_5_cout,
       n1_bit_alu_6_cout, n1_bit_alu_7_cout, n1_bit_alu_8_cout, n1_bit_alu_9_cout, n1_bit_alu_10_cout,
       n1_bit_alu_11_cout, n1_bit_alu_12_cout, n1_bit_alu_13_cout, n1_bit_alu_14_cout, n1_bit_alu_15_cout,
       opdec_1_ainv, opdec_1_binv, opdec_1_cout;
  wire [1:0] opdec_1_op;

  opdec opdec_1 (.in_1(Operation), .op(opdec_1_op), .binv(opdec_1_binv), .cout(opdec_1_cout), .ainv(opdec_1_ainv));
  _1_bit_alu u_1_bit_alu_1 (
    .ain(fin[0]), .bin(sin[0]), .less(out_5[15]), .out_8(out_5[0]), .binv(opdec_1_binv), .ainv(opdec_1_ainv),
    .cin(opdec_1_cout), .op(opdec_1_op), .cout(n1_bit_alu_1_cout));
  _1_bit_alu u_1_bit_alu_2 (
    .ain(fin[1]), .bin(sin[1]), .less(1'b0), .out_8(out_5[1]), .binv(opdec_1_binv), .ainv(opdec_1_ainv),
    .cin(n1_bit_alu_1_cout), .op(opdec_1_op), .cout(n1_bit_alu_2_cout));
  _1_bit_alu u_1_bit_alu_3 (
    .ain(fin[2]), .bin(sin[2]), .less(1'b0), .out_8(out_5[2]), .binv(opdec_1_binv), .ainv(opdec_1_ainv),
    .cin(n1_bit_alu_2_cout), .op(opdec_1_op), .cout(n1_bit_alu_3_cout));
  _1_bit_alu u_1_bit_alu_4 (
    .ain(fin[3]), .bin(sin[3]), .less(1'b0), .out_8(out_5[3]), .binv(opdec_1_binv), .ainv(opdec_1_ainv),
    .cin(n1_bit_alu_3_cout), .op(opdec_1_op), .cout(n1_bit_alu_4_cout));
  _1_bit_alu u_1_bit_alu_5 (
    .ain(fin[4]), .bin(sin[4]), .less(1'b0), .out_8(out_5[4]), .binv(opdec_1_binv), .ainv(opdec_1_ainv),
    .cin(n1_bit_alu_4_cout), .op(opdec_1_op), .cout(n1_bit_alu_5_cout));
  _1_bit_alu u_1_bit_alu_6 (
    .ain(fin[5]), .bin(sin[5]), .less(1'b0), .out_8(out_5[5]), .binv(opdec_1_binv), .ainv(opdec_1_ainv),
    .cin(n1_bit_alu_5_cout), .op(opdec_1_op), .cout(n1_bit_alu_6_cout));
  _1_bit_alu u_1_bit_alu_7 (
    .ain(fin[6]), .bin(sin[6]), .less(1'b0), .out_8(out_5[6]), .binv(opdec_1_binv), .ainv(opdec_1_ainv),
    .cin(n1_bit_alu_6_cout), .op(opdec_1_op), .cout(n1_bit_alu_7_cout));
  _1_bit_alu u_1_bit_alu_8 (
    .ain(fin[7]), .bin(sin[7]), .less(1'b0), .out_8(out_5[7]), .binv(opdec_1_binv), .ainv(opdec_1_ainv),
    .cin(n1_bit_alu_7_cout), .op(opdec_1_op), .cout(n1_bit_alu_8_cout));
  _1_bit_alu u_1_bit_alu_9 (
    .ain(fin[8]), .bin(sin[8]), .less(1'b0), .out_8(out_5[8]), .binv(opdec_1_binv), .ainv(opdec_1_ainv),
    .cin(n1_bit_alu_8_cout), .op(opdec_1_op), .cout(n1_bit_alu_9_cout));
  _1_bit_alu u_1_bit_alu_10 (
    .ain(fin[9]), .bin(sin[9]), .less(1'b0), .out_8(out_5[9]), .binv(opdec_1_binv), .ainv(opdec_1_ainv),
    .cin(n1_bit_alu_9_cout), .op(opdec_1_op), .cout(n1_bit_alu_10_cout));
  _1_bit_alu u_1_bit_alu_11 (
    .ain(fin[10]), .bin(sin[10]), .less(1'b0), .out_8(out_5[10]), .binv(opdec_1_binv), .ainv(opdec_1_ainv),
    .cin(n1_bit_alu_10_cout), .op(opdec_1_op), .cout(n1_bit_alu_11_cout));
  _1_bit_alu u_1_bit_alu_12 (
    .ain(fin[11]), .bin(sin[11]), .less(1'b0), .out_8(out_5[11]), .binv(opdec_1_binv), .ainv(opdec_1_ainv),
    .cin(n1_bit_alu_11_cout), .op(opdec_1_op), .cout(n1_bit_alu_12_cout));
  _1_bit_alu u_1_bit_alu_13 (
    .ain(fin[12]), .bin(sin[12]), .less(1'b0), .out_8(out_5[12]), .binv(opdec_1_binv), .ainv(opdec_1_ainv),
    .cin(n1_bit_alu_12_cout), .op(opdec_1_op), .cout(n1_bit_alu_13_cout));
  _1_bit_alu u_1_bit_alu_14 (
    .ain(fin[13]), .bin(sin[13]), .less(1'b0), .out_8(out_5[13]), .binv(opdec_1_binv), .ainv(opdec_1_ainv),
    .cin(n1_bit_alu_13_cout), .op(opdec_1_op), .cout(n1_bit_alu_14_cout));
  _1_bit_alu u_1_bit_alu_15 (
    .ain(fin[14]), .bin(sin[14]), .less(1'b0), .out_8(out_5[14]), .binv(opdec_1_binv), .ainv(opdec_1_ainv),
    .cin(n1_bit_alu_14_cout), .op(opdec_1_op), .cout(n1_bit_alu_15_cout));
  _1_bit_alu u_1_bit_alu_16 (
    .ain(fin[15]), .bin(sin[15]), .less(1'b0), .out_8(out_5[15]), .binv(opdec_1_binv), .ainv(opdec_1_ainv),
    .cin(n1_bit_alu_15_cout), .op(opdec_1_op));  // open: cout
  nor nor_1 (zero, out_5[0], out_5[15], out_5[1], out_5[2], out_5[3], out_5[4], out_5[5], out_5[6], out_5[7], out_5[8], out_5[9], out_5[10], out_5[11], out_5[12], out_5[13], out_5[14]);
  xnor xnor_1 (gtz, fin[15], 1'b0);
endmodule

module _1_bit_alu (
  input  binv,
  input  ainv,
  input  cin,
  input  [1:0] op,
  input  ain,
  input  bin,
  input  less,
  output out_8,
  output cout
);

  wire adder_1_out, and_1_out, multiplexer_1_out, multiplexer_2_out, not_1_out, not_2_out, or_1_out;

  not not_1 (not_1_out, ain);
  not not_2 (not_2_out, bin);
  Multiplexer multiplexer_1 (.in0(ain), .in1(not_1_out), .out(multiplexer_1_out), .sel(ainv));  // open: en
  Multiplexer multiplexer_2 (.in0(bin), .in1(not_2_out), .out(multiplexer_2_out), .sel(binv));  // open: en
  and and_1 (and_1_out, multiplexer_1_out, multiplexer_2_out);
  or or_1 (or_1_out, multiplexer_1_out, multiplexer_2_out);
  Adder #(.width(1)) adder_1 (.a(multiplexer_1_out), .b(multiplexer_2_out), .out(adder_1_out), .cin(cin), .cout(cout));
  Multiplexer #(.select(2)) multiplexer_3 (
    .in0(and_1_out), .in1(or_1_out), .in2(adder_1_out), .in3(less), .out(out_8), .sel(op));  // open: en
endmodule

module opdec (
  input  [3:0] in_1,
  output [1:0] op,
  output binv,
  output ainv,
  output cout
);

  wire not_1_out, not_2_out;

  or or_1 (op[1], in_1[1], in_1[2]);
  not not_1 (not_1_out, in_1[0]);
  and and_1 (binv, not_1_out, in_1[1], in_1[2]);
  and and_2 (cout, in_1[1], in_1[2], not_2_out);
  not not_2 (not_2_out, in_1[0]);

  assign ainv = 1'b0;
  assign op[0] = in_1[0];
endmodule

module as (
  input  [1:0] in_1,
  input  [15:0] in_2,
  input  [15:0] in_3,
  input  [15:0] in_4,
  input  [15:0] in_5,
  input  in_6,
  output [15:0] out_7
);

  // XNOR_Gate xnor_1 has open pins: in0=in_6, in1=1'b0, out=open
  Multiplexer #(.select(2), .width(16)) multiplexer_1 (
    .in0(in_2), .in1(in_3), .in2(in_4), .in3(in_5), .out(out_7), .sel(in_1));  // open: en
endmodule
